// Logisim project IFU.circ as structural Verilog: 1 circuit, main circuit IFU
module IFU (
  input  Clock,
  input  Reset,
  output [31:0] Instruction
);

  wire [31:0] n32_bit_adder_1_s, PC_q;

  Register #(.width(32)) PC (.D(n32_bit_adder_1_s), .Q(PC_q), .clk(Clock), .clr(Reset));  // open: en
  _32_bit_adder u_32_bit_adder_1 (.A(PC_q), .B(32'h4), .S(n32_bit_adder_1_s));  // open: Cin, Cout
  ROM #(.addrWidth(5), .dataWidth(32)) rom_1 (.addr(PC_q[6:2]), .data(Instruction));  // open: sel
endmodule
